# Fritzing sketch Photoresistance (saved by Fritzing 0.9.2b)
breadboards: 1

parts:
  Part1 = Arduino Uno (Rev3) - ICSP
  R3 = Photocell (LDR) [package=THT]
  R4 = Resistor [tolerance=±5% resistance=220 package="2010 [SMD]"]

nets:
  N1: Part1.A0, R3.pin_0, R4.Pin_1
  N2: Part1.5V, R3.pin_1
  N3: Part1.GND, R4.Pin_0

notes:
  Lecture sur connecteur A0
