# Fritzing sketch sens du courant (saved by Fritzing 0.9.2b)
breadboards: 1

parts:
  LED1 = smd LED [color="Red (633nm)" package="0603 [SMD]"]
  U1 = BATTERY-2 [package=battery-aa]  # not connected
  R1 = Resistor [tolerance=±5% resistance=220 package="0402 [SMD]"]

nets:
  N1: LED1.cathode, LED1.anode, R1.Pin_0
