# Fritzing sketch Theremine (saved by Fritzing 0.9.2b)
breadboards: 1

parts:
  Part1 = Arduino Uno (Rev3) - ICSP
  SG3 = Buzzer 12mm [package=buzzer-12mm]
  R3 = Photocell (LDR) [package=THT]
  R4 = Resistor [tolerance=±5% resistance=220 package="2010 [SMD]"]
  R5 = Resistor [tolerance=±5% resistance=220 package=THT]

nets:
  N1: Part1.A0, R3.pin_1, R4.Pin_0
  N2: Part1.D8, R5.Pin_0
  N3: Part1.GND, SG3.2
  N4: Part1.5V, R3.pin_0
  N5: SG3.1, R5.Pin_1
