# Fritzing sketch SchemaCircuit-Emetteur-Morse (saved by Fritzing 0.9.2b)
breadboards: 1

parts:
  Part1 = Arduino Uno (Rev3) - ICSP
  LED1 = smd LED [color="Red (633nm)" package="0805 [SMD]"]  # not connected
  S1 = SWITCH-MOMENTARY-2 [package=tactile-pth]  # not connected
  R1 = Resistor [tolerance=±5% resistance=220 package=THT]

nets:
  N1: Part1.GND, R1.Pin_1
