# Fritzing sketch SchemaCircuit-Interrupteur (saved by Fritzing 0.9.2b)
breadboards: 1

parts:
  Part1 = Arduino Uno (Rev3) - ICSP
  R2 = Resistor [tolerance=±5% resistance=220 package=THT]
  SG3 = Buzzer 12mm [package=buzzer-12mm]
  R3 = Resistor [tolerance=±5% resistance=220 package=THT]
  LED1 = smd LED [color="Red (633nm)" package="0805 [SMD]"]
  S1 = SWITCH-MOMENTARY-2 [package=tactile-pth]

nets:
  N1: Part1.D8, SG3.2, LED1.anode
  N2: Part1.GND, R2.Pin_1, R3.Pin_1, S1.2
  N3: R2.Pin_0, SG3.1
  N4: R3.Pin_0, LED1.cathode
