# Fritzing sketch Circuit-2LED (saved by Fritzing 0.9.2b)
breadboards: 1

parts:
  Part1 = Arduino Uno (Rev3)
  LED1 = smd LED [color="Red (633nm)" package="1206 [SMD]"]
  LED2 = smd LED [color="Red (633nm)" package="1206 [SMD]"]
  R1 = Resistor [tolerance=±5% resistance=220 package=THT]
  R2 = Resistor [tolerance=±5% resistance=220 package=THT]

nets:
  N1: Part1.D12/MISO, LED2.anode
  N2: Part1.D13/SCK, LED1.anode
  N3: Part1.GND, R1.Pin_1, R2.Pin_1
  N4: LED1.cathode, R1.Pin_0
  N5: LED2.cathode, R2.Pin_0

notes:
  Rouge / Vert
