# Fritzing sketch SchemaCircuit-Emetteur-Morse-Sonore (saved by Fritzing 0.9.2b)
breadboards: 1

parts:
  Part1 = Arduino Uno (Rev3) - ICSP
  R2 = Resistor [tolerance=±5% resistance=220 package=THT]
  SG3 = Buzzer 12mm [package=buzzer-12mm]
  R3 = Resistor [tolerance=±5% resistance=220 package=THT]
  LED1 = smd LED [color="Red (633nm)" package="0805 [SMD]"]
  S1 = SWITCH-MOMENTARY-2 [package=tactile-pth]
  R4 = Resistor [tolerance=±5% resistance=220 package=THT]

nets:
  N1: Part1.GND, R2.Pin_0, R3.Pin_0, R4.Pin_0
  N2: Part1.D8, SG3.1
  N3: Part1.D13/SCK, LED1.anode
  N4: Part1.5V, S1.2
  N5: R2.Pin_1, LED1.cathode
  N6: SG3.2, R3.Pin_1
