# Fritzing sketch SchemaCircuit-Buzzer (saved by Fritzing 0.9.2b)
breadboards: 1

parts:
  Part1 = Arduino Uno (Rev3) - ICSP
  R2 = Resistor [tolerance=±5% resistance=220 package=THT]
  SG3 = Buzzer 12mm [package=buzzer-12mm]

nets:
  N1: Part1.D8, R2.Pin_1
  N2: Part1.GND, SG3.2
  N3: R2.Pin_0, SG3.1
